# Fritzing sketch IR_emitter (saved by Fritzing 0.9.5d)

parts:
  Raspberry_Pi = Raspberry Pi 3 [part_number=RPI-3-V1.2]
  LED = LED - 5mm [color="Infrared (940nm)" package="5 mm [THT]"]
  R1 = Resistor [tolerance=±5% resistance=50 package=THT]

nets:
  N1: Raspberry_Pi.GND, LED.cathode
  N2: Raspberry_Pi.GPIO18, R1.Pin_0
  N3: LED.anode, R1.Pin_1

notes:
  GND
  GPIO18
